// Logisim project FPU.circ as structural Verilog: 5 circuits, main circuit main
module main (
  input  [31:0] a,
  input  [1:0] c,
  input  [31:0] b,
  output [31:0] o
);

  wire [31:0] fpu_adder_56b1aa8a_1_output, fpu_divider_2c30928d_1_output, fpu_multiplier_a4ba9898_1_output,
       fpu_subtractor_be9453c3_1_output;

  FPU_Adder_56b1aa8a fpu_adder_56b1aa8a_1 (.A(a), .B(b), .Output(fpu_adder_56b1aa8a_1_output));  // open: Overflow
  FPU_Subtractor_be9453c3 fpu_subtractor_be9453c3_1 (
    .A(a), .B(b), .Output(fpu_subtractor_be9453c3_1_output));  // open: Overflow, Underflow
  FPU_Multiplier_a4ba9898 fpu_multiplier_a4ba9898_1 (
    .A(a), .B(b), .Output(fpu_multiplier_a4ba9898_1_output));  // open: Overflow
  FPU_divider_2c30928d fpu_divider_2c30928d_1 (
    .A(a), .B(b), .Output(fpu_divider_2c30928d_1_output));  // open: Divide_by_Zero_0569a107
  Multiplexer #(.select(2), .width(32)) multiplexer_1 (
    .in0(fpu_adder_56b1aa8a_1_output), .in1(fpu_subtractor_be9453c3_1_output),
    .in2(fpu_multiplier_a4ba9898_1_output), .in3(fpu_divider_2c30928d_1_output), .out(o), .sel(c));  // open: en

  // Notes on the sheet:
  //   Control bits:
  //   00: Adder
  //   01:Subtractor
  //   10:Multiplier
  //   11: Divider
  //   Input1
  //   Input2
  //   ADDER
  //   Subtractor
  //   Multiplier
  //   Divider
  //   Control bit 
  //   Output
endmodule

module FPU_Adder_56b1aa8a (
  input  [31:0] A,
  input  [31:0] B,
  output [31:0] Output,
  output Overflow
);

  wire adder_3_cout, comparator_1_gt, comparator_2_eq, comparator_3_gt, multiplexer_3_out;
  wire [7:0] adder_1_out, adder_2_out, multiplexer_1_out, multiplexer_2_out, subtractor_1_out,
       subtractor_2_out, subtractor_3_out;

  // Probe on A
  // Probe on B
  xor xor_1 (Output[31], B[31], A[31]);
  Comparator comparator_1 (.a(A[30:23]), .b(B[30:23]), .gt(comparator_1_gt));  // open: eq, lt
  Adder adder_1 (.a(A[30:23]), .b(8'h1), .out(adder_1_out));  // open: cin, cout
  Adder adder_2 (.a(B[30:23]), .b(8'h1), .out(adder_2_out));  // open: cin, cout
  Adder #(.width(23)) adder_3 (.a(A[22:0]), .b(B[22:0]), .out(Output[22:0]), .cout(adder_3_cout));  // open: cin
  Multiplexer #(.width(8), .enable("false")) multiplexer_1 (
    .in0(adder_1_out), .in1(adder_2_out), .out(multiplexer_1_out), .sel(comparator_1_gt));
  Multiplexer #(.width(8), .enable("false")) multiplexer_2 (
    .in0(A[30:23]), .in1(B[30:23]), .out(multiplexer_2_out), .sel(comparator_1_gt));
  Comparator #(.width(1)) comparator_2 (.a(adder_3_cout), .b(1'b0), .eq(comparator_2_eq));  // open: gt, lt
  Subtractor subtractor_1 (.a(B[30:23]), .b(A[30:23]), .out(subtractor_1_out));  // open: bin, bout
  Comparator comparator_3 (.a(multiplexer_1_out), .b({8{1'b1}}), .gt(comparator_3_gt));  // open: eq, lt
  Subtractor subtractor_2 (.a({8{1'b0}}), .b(subtractor_1_out), .out(subtractor_2_out));  // open: bin, bout
  Multiplexer #(.enable("false")) multiplexer_3 (
    .in0(1'b1), .in1(1'b0), .out(multiplexer_3_out), .sel(comparator_3_gt));
  Subtractor subtractor_3 (.a(multiplexer_2_out), .b(subtractor_2_out), .out(subtractor_3_out));  // open: bin, bout
  Multiplexer #(.width(8), .enable("false")) multiplexer_4 (
    .in0(multiplexer_1_out), .in1(subtractor_3_out), .out(Output[30:23]), .sel(comparator_2_eq));
  and and_1 (Overflow, multiplexer_3_out, Output[31]);
  // Probe on Output
endmodule

module FPU_Subtractor_be9453c3 (
  input  [31:0] A,
  input  [31:0] B,
  output [31:0] Output,
  output Overflow,
  output Underflow
);

  wire comparator_1_gt, comparator_2_eq, comparator_3_lt, comparator_4_gt, multiplexer_4_out,
       multiplexer_5_out, not_1_out, subtractor_1_bout;
  wire [7:0] adder_1_out, adder_2_out, adder_3_out, multiplexer_1_out, multiplexer_2_out, multiplexer_3_out,
       subtractor_2_out, subtractor_3_out;

  // Probe on A
  // Probe on B
  xor xor_1 (Output[31], B[31], A[31]);
  Comparator comparator_1 (.a(A[30:23]), .b(B[30:23]), .gt(comparator_1_gt));  // open: eq, lt
  Adder adder_1 (.a(A[30:23]), .b(8'h1), .out(adder_1_out));  // open: cin, cout
  Adder adder_2 (.a(B[30:23]), .b(8'h1), .out(adder_2_out));  // open: cin, cout
  not not_1 (not_1_out, comparator_1_gt);
  Subtractor #(.width(23)) subtractor_1 (
    .a(A[22:0]), .b(B[22:0]), .out(Output[22:0]), .bout(subtractor_1_bout));  // open: bin
  Multiplexer #(.width(8), .enable("false")) multiplexer_1 (
    .in0(adder_1_out), .in1(adder_2_out), .out(multiplexer_1_out), .sel(comparator_1_gt));
  Multiplexer #(.width(8), .enable("false")) multiplexer_2 (
    .in0(A[30:23]), .in1(B[30:23]), .out(multiplexer_2_out), .sel(comparator_1_gt));
  Multiplexer #(.width(8), .enable("false")) multiplexer_3 (
    .in0(A[30:23]), .in1(B[30:23]), .out(multiplexer_3_out), .sel(not_1_out));
  Comparator #(.width(1)) comparator_2 (.a(subtractor_1_bout), .b(1'b0), .eq(comparator_2_eq));  // open: gt, lt
  Subtractor subtractor_2 (.a(B[30:23]), .b(A[30:23]), .out(subtractor_2_out));  // open: bin, bout
  Comparator comparator_3 (.a(multiplexer_2_out), .b({8{1'b0}}), .lt(comparator_3_lt));  // open: gt, eq
  Comparator comparator_4 (.a(multiplexer_3_out), .b({8{1'b1}}), .gt(comparator_4_gt));  // open: eq, lt
  Subtractor subtractor_3 (.a({8{1'b0}}), .b(subtractor_2_out), .out(subtractor_3_out));  // open: bin, bout
  Multiplexer #(.enable("false")) multiplexer_4 (
    .in0(1'b1), .in1(1'b0), .out(multiplexer_4_out), .sel(comparator_3_lt));
  Multiplexer #(.enable("false")) multiplexer_5 (
    .in0(1'b1), .in1(1'b0), .out(multiplexer_5_out), .sel(comparator_4_gt));
  Adder adder_3 (.a(multiplexer_2_out), .b(subtractor_3_out), .out(adder_3_out));  // open: cin, cout
  and and_1 (Underflow, Output[31], multiplexer_5_out);
  Multiplexer #(.width(8), .enable("false")) multiplexer_6 (
    .in0(multiplexer_1_out), .in1(adder_3_out), .out(Output[30:23]), .sel(comparator_2_eq));
  and and_2 (Overflow, multiplexer_4_out, Output[31]);
  // Probe on Output
endmodule

module FPU_Multiplier_a4ba9898 (
  input  [31:0] A,
  input  [31:0] B,
  output [31:0] Output,
  output Overflow
);

  wire comparator_1_eq;
  wire [7:0] adder_1_out;

  // Probe on A
  // Probe on B
  xor xor_1 (Output[31], B[31], A[31]);
  Adder adder_1 (.a(A[30:23]), .b(B[30:23]), .out(adder_1_out));  // open: cin, cout
  Multiplier #(.width(23)) multiplier_1 (.a(A[22:0]), .b(B[22:0]), .out(Output[22:0]));  // open: cin, cout
  Subtractor subtractor_1 (.a(adder_1_out), .b(8'h7f), .out(Output[30:23]));  // open: bin, bout
  Comparator comparator_1 (.a(Output[30:23]), .b({8{1'b1}}), .eq(comparator_1_eq));  // open: gt, lt
  // Probe on Output
  Multiplexer #(.enable("false")) multiplexer_1 (.in0(1'b0), .in1(1'b1), .out(Overflow), .sel(comparator_1_eq));
endmodule

module FPU_divider_2c30928d (
  input  [31:0] A,
  input  [31:0] B,
  output [31:0] Output,
  output Divide_by_Zero_0569a107
);

  wire comparator_1_eq;
  wire [7:0] subtractor_1_out, subtractor_2_out;

  // Probe on A
  // Probe on B
  xor xor_1 (Output[31], B[31], A[31]);
  Comparator comparator_1 (.a(B[30:23]), .b({8{1'b0}}), .eq(comparator_1_eq));  // open: gt, lt
  Subtractor subtractor_1 (.a(A[30:23]), .b(8'h7f), .out(subtractor_1_out));  // open: bin, bout
  Subtractor subtractor_2 (.a(B[30:23]), .b(8'h7f), .out(subtractor_2_out));  // open: bin, bout
  Divider #(.width(23)) divider_1 (.a(A[22:0]), .b(B[22:0]), .out(Output[22:0]));  // open: upper, rem
  Adder adder_1 (.a(subtractor_1_out), .b(subtractor_2_out), .out(Output[30:23]));  // open: cin, cout
  Multiplexer #(.enable("false")) multiplexer_1 (
    .in0(1'b0), .in1(1'b1), .out(Divide_by_Zero_0569a107), .sel(comparator_1_eq));
  // Probe on Output

  // Notes on the sheet:
  //   Dividing Significands
  //   Adding Exponents
  //   Rounding
endmodule
